// Logisim project CPU_RISC_V_versao3.circ as structural Verilog
module Teste (
  input  [31:0] in_1,
  input  [31:0] A,
  input  [1:0] in_3,
  input  [31:0] B,
  input  [31:0] in_5,
  input  in_6,
  input  [31:0] in_7,
  input  [3:0] in_8,
  input  in_9,
  input  [31:0] in_10,
  input  in_11,
  input  [31:0] in_12,
  input  [31:0] in_13,
  output [3:0] out_14,
  output [31:0] Z,
  output out_16,
  output [1:0] out_17,
  output [31:0] out_18,
  output out_19,
  output out_20,
  output out_21,
  output out_22,
  output out_23,
  output out_24,
  output [31:0] out_25,
  output [31:0] out_26,
  output [31:0] out_27
);

  wire clock_1_out, clock_2_out;

  Clock clock_1 (.out(clock_1_out));
  ALU2 alu2_1 (.A(A), .B(B), .Control(in_8), .Result(Z), .Zero(out_16));
  ImmGen immgen_1 (.Instr(in_10), .Imm(out_26));
  PC2 pc2_1 (.clk(clock_1_out), .rst(in_11), .PC_in(in_12), .PC_out(out_27));
  ALUControl alucontrol_1 (.Instr(in_1), .ALUOp(in_3), .Control(out_14));
  control_unit control_unit_1 (
    .Instr(in_5), .ALUOp(out_17), .ALUSrc(out_19), .Branch(out_20), .MemRead(out_21), .MemWrite(out_22),
    .RegWrite(out_23), .MemtoReg(out_24));
  Clock clock_2 (.out(clock_2_out));
  regiters regiters_1 (
    .ReadReg1(in_13[20:16]), .ReadReg2(in_13[25:21]), .RegWrite(in_9), .WriteReg(in_13[12:8]), .rst(in_6),
    .clk(clock_2_out), .WriteData(in_7), .ReadData1(out_18), .ReadData2(out_25));

  // Notes on the sheet:
  //   PC_in -> rising clock -> PC_out
  //   0x00100113 -> ADDI: 000000000001
  //   Instr[0:6] = 0110011
  //   (Instr[12:14] = 101) + (ALUOp = 11) -> 0110 (SLRI)
  //   (Instr[12:14] = 0) + (Instr[30] = 1) + (ALUOp = 10) -> 0001 (SUB)
endmodule

module regiters (
  input  [31:0] WriteData,
  input  rst,
  input  clk,
  input  RegWrite,
  input  [4:0] WriteReg,
  input  [4:0] ReadReg1,
  input  [4:0] ReadReg2,
  output [31:0] ReadData1,
  output [31:0] ReadData2
);

  wire demultiplexer_1_out0, demultiplexer_1_out1, demultiplexer_1_out2, demultiplexer_1_out3,
       demultiplexer_1_out4, demultiplexer_1_out5, demultiplexer_1_out6, demultiplexer_1_out7,
       demultiplexer_1_out8, demultiplexer_1_out9, demultiplexer_1_out10, demultiplexer_1_out11,
       demultiplexer_1_out12, demultiplexer_1_out13, demultiplexer_1_out14, demultiplexer_1_out15,
       demultiplexer_1_out16, demultiplexer_1_out17, demultiplexer_1_out18, demultiplexer_1_out19,
       demultiplexer_1_out20, demultiplexer_1_out21, demultiplexer_1_out22, demultiplexer_1_out23,
       demultiplexer_1_out24, demultiplexer_1_out25, demultiplexer_1_out26, demultiplexer_1_out27,
       demultiplexer_1_out28, demultiplexer_1_out29, demultiplexer_1_out30, demultiplexer_1_out31;
  wire [31:0] multiplexer_1_out, multiplexer_2_out, R0_q, R1_q, R2_q, R3_q, R4_q, R5_q, R6_q, R7_q, R8_q,
       R9_q, R10_q, R11_q, R12_q, R13_q, R14_q, R15_q, R16_q, R17_q, R18_q, R19_q, R20_q, R21_q, R22_q,
       R23_q, R24_q, R25_q, R26_q, R27_q, R28_q, R29_q, R30_q, R31_q;

  Demultiplexer #(.select(5)) demultiplexer_1 (
    .out0(demultiplexer_1_out0), .out1(demultiplexer_1_out1), .out2(demultiplexer_1_out2),
    .out3(demultiplexer_1_out3), .out4(demultiplexer_1_out4), .out5(demultiplexer_1_out5),
    .out6(demultiplexer_1_out6), .out7(demultiplexer_1_out7), .out8(demultiplexer_1_out8),
    .out9(demultiplexer_1_out9), .out10(demultiplexer_1_out10), .out11(demultiplexer_1_out11),
    .out12(demultiplexer_1_out12), .out13(demultiplexer_1_out13), .out14(demultiplexer_1_out14),
    .out15(demultiplexer_1_out15), .out16(demultiplexer_1_out16), .out17(demultiplexer_1_out17),
    .out18(demultiplexer_1_out18), .out19(demultiplexer_1_out19), .out20(demultiplexer_1_out20),
    .out21(demultiplexer_1_out21), .out22(demultiplexer_1_out22), .out23(demultiplexer_1_out23),
    .out24(demultiplexer_1_out24), .out25(demultiplexer_1_out25), .out26(demultiplexer_1_out26),
    .out27(demultiplexer_1_out27), .out28(demultiplexer_1_out28), .out29(demultiplexer_1_out29),
    .out30(demultiplexer_1_out30), .out31(demultiplexer_1_out31), .in(RegWrite), .sel(WriteReg));
  Register #(.width(32)) R0 (.D(WriteData), .en(demultiplexer_1_out0), .clk(clk), .Q(R0_q), .clr(rst));
  Register #(.width(32)) R8 (.D(WriteData), .en(demultiplexer_1_out8), .clk(clk), .Q(R8_q), .clr(rst));
  Register #(.width(32)) R16 (.D(WriteData), .en(demultiplexer_1_out16), .clk(clk), .Q(R16_q), .clr(rst));
  Register #(.width(32)) R24 (.D(WriteData), .en(demultiplexer_1_out24), .clk(clk), .Q(R24_q), .clr(rst));
  Register #(.width(32)) R1 (.D(WriteData), .en(demultiplexer_1_out1), .clk(clk), .Q(R1_q), .clr(rst));
  Register #(.width(32)) R9 (.D(WriteData), .en(demultiplexer_1_out9), .clk(clk), .Q(R9_q), .clr(rst));
  Register #(.width(32)) R17 (.D(WriteData), .en(demultiplexer_1_out17), .clk(clk), .Q(R17_q), .clr(rst));
  Register #(.width(32)) R25 (.D(WriteData), .en(demultiplexer_1_out25), .clk(clk), .Q(R25_q), .clr(rst));
  Register #(.width(32)) R2 (.D(WriteData), .en(demultiplexer_1_out2), .clk(clk), .Q(R2_q), .clr(rst));
  Register #(.width(32)) R10 (.D(WriteData), .en(demultiplexer_1_out10), .clk(clk), .Q(R10_q), .clr(rst));
  Register #(.width(32)) R18 (.D(WriteData), .en(demultiplexer_1_out18), .clk(clk), .Q(R18_q), .clr(rst));
  Register #(.width(32)) R26 (.D(WriteData), .en(demultiplexer_1_out26), .clk(clk), .Q(R26_q), .clr(rst));
  Register #(.width(32)) R11 (.D(WriteData), .en(demultiplexer_1_out11), .clk(clk), .Q(R11_q), .clr(rst));
  Register #(.width(32)) R19 (.D(WriteData), .en(demultiplexer_1_out19), .clk(clk), .Q(R19_q), .clr(rst));
  Register #(.width(32)) R3 (.D(WriteData), .en(demultiplexer_1_out3), .clk(clk), .Q(R3_q), .clr(rst));
  Register #(.width(32)) R27 (.D(WriteData), .en(demultiplexer_1_out27), .clk(clk), .Q(R27_q), .clr(rst));
  Register #(.width(32)) R4 (.D(WriteData), .en(demultiplexer_1_out4), .clk(clk), .Q(R4_q), .clr(rst));
  Register #(.width(32)) R12 (.D(WriteData), .en(demultiplexer_1_out12), .clk(clk), .Q(R12_q), .clr(rst));
  Register #(.width(32)) R20 (.D(WriteData), .en(demultiplexer_1_out20), .clk(clk), .Q(R20_q), .clr(rst));
  Register #(.width(32)) R28 (.D(WriteData), .en(demultiplexer_1_out28), .clk(clk), .Q(R28_q), .clr(rst));
  Register #(.width(32)) R5 (.D(WriteData), .en(demultiplexer_1_out5), .clk(clk), .Q(R5_q), .clr(rst));
  Register #(.width(32)) R13 (.D(WriteData), .en(demultiplexer_1_out13), .clk(clk), .Q(R13_q), .clr(rst));
  Register #(.width(32)) R21 (.D(WriteData), .en(demultiplexer_1_out21), .clk(clk), .Q(R21_q), .clr(rst));
  Register #(.width(32)) R29 (.D(WriteData), .en(demultiplexer_1_out29), .clk(clk), .Q(R29_q), .clr(rst));
  Register #(.width(32)) R6 (.D(WriteData), .en(demultiplexer_1_out6), .clk(clk), .Q(R6_q), .clr(rst));
  Register #(.width(32)) R14 (.D(WriteData), .en(demultiplexer_1_out14), .clk(clk), .Q(R14_q), .clr(rst));
  Register #(.width(32)) R22 (.D(WriteData), .en(demultiplexer_1_out22), .clk(clk), .Q(R22_q), .clr(rst));
  Register #(.width(32)) R30 (.D(WriteData), .en(demultiplexer_1_out30), .clk(clk), .Q(R30_q), .clr(rst));
  Register #(.width(32)) R7 (.D(WriteData), .en(demultiplexer_1_out7), .clk(clk), .Q(R7_q), .clr(rst));
  Register #(.width(32)) R15 (.D(WriteData), .en(demultiplexer_1_out15), .clk(clk), .Q(R15_q), .clr(rst));
  Register #(.width(32)) R23 (.D(WriteData), .en(demultiplexer_1_out23), .clk(clk), .Q(R23_q), .clr(rst));
  Register #(.width(32)) R31 (.D(WriteData), .en(demultiplexer_1_out31), .clk(clk), .Q(R31_q), .clr(rst));
  Multiplexer #(.select(5), .width(32)) multiplexer_1 (
    .in0(R0_q), .in1(R1_q), .in2(R2_q), .in3(R3_q), .in4(R4_q), .in5(R5_q), .in6(R6_q), .in7(R7_q),
    .in8(R8_q), .in9(R9_q), .in10(R10_q), .in11(R11_q), .in12(R12_q), .in13(R13_q), .in14(R14_q),
    .in15(R15_q), .in16(R16_q), .in17(R17_q), .in18(R18_q), .in19(R19_q), .in20(R20_q), .in21(R21_q),
    .in22(R22_q), .in23(R23_q), .in24(R24_q), .in25(R25_q), .in26(R26_q), .in27(R27_q), .in28(R28_q),
    .in29(R29_q), .in30(R30_q), .in31(R31_q), .out(multiplexer_1_out), .sel(ReadReg1));
  Multiplexer #(.select(5), .width(32)) multiplexer_2 (
    .in0(R0_q), .in1(R1_q), .in2(R2_q), .in3(R3_q), .in4(R4_q), .in5(R5_q), .in6(R6_q), .in7(R7_q),
    .in8(R8_q), .in9(R9_q), .in10(R10_q), .in11(R11_q), .in12(R12_q), .in13(R13_q), .in14(R14_q),
    .in15(R15_q), .in16(R16_q), .in17(R17_q), .in18(R18_q), .in19(R19_q), .in20(R20_q), .in21(R21_q),
    .in22(R22_q), .in23(R23_q), .in24(R24_q), .in25(R25_q), .in26(R26_q), .in27(R27_q), .in28(R28_q),
    .in29(R29_q), .in30(R30_q), .in31(R31_q), .out(multiplexer_2_out), .sel(ReadReg2));
  Register #(.width(32)) register_1 (.D(multiplexer_1_out), .en(1'b1), .clk(clk), .Q(ReadData1), .clr(rst));
  Register #(.width(32)) register_2 (.D(multiplexer_2_out), .en(1'b1), .clk(clk), .Q(ReadData2), .clr(rst));
endmodule

module IF_ID_Pipeline (
  input  clk,
  input  rst,
  input  IF_ID_Write,
  input  IF_ID_Flush,
  input  [31:0] PC_in,
  input  [63:0] PC_4_in,
  input  [31:0] Instr_in,
  output [31:0] PC_out,
  output [63:0] PC_4_out,
  output [31:0] Instr_out
);

  IF_ID_Pipe if_id_pipe_1 (
    .clk(clk), .rst(rst), .IF_ID_Write(IF_ID_Write), .IF_ID_Flush(IF_ID_Flush), .PC_in(PC_in),
    .PC_4_in(PC_4_in), .Instr_in(Instr_in), .PC_out(PC_out), .PC_4_out(PC_4_out), .Instr_out(Instr_out));
endmodule

module ID_EX_Pipeline (
  input  clk,
  input  rst,
  input  [31:0] PC_in,
  input  [31:0] RD1_in,
  input  [31:0] RD2_in,
  input  [31:0] SE_in,
  input  [4:0] Rs_in,
  input  [4:0] Rt_in,
  input  [4:0] Rd_in,
  input  [3:0] Control_in,
  output [31:0] PC_out,
  output [31:0] RD1_out,
  output [31:0] RD2_out,
  output [31:0] Se_out,
  output [4:0] Rs_out,
  output [4:0] Rt_out,
  output [4:0] Rd_out,
  output [3:0] Control_out
);

  ID_EX id_ex_1 (
    .clk(clk), .rst(rst), .PC_in(PC_in), .ReadData1_in(RD1_in), .ReadData2_in(RD2_in), .SignExtend_in(SE_in),
    .Rs_in(Rs_in), .Rt_in(Rt_in), .Rd_in(Rd_in), .Control_in(Control_in), .PC_out(PC_out),
    .ReadData1_out(RD1_out), .ReadData2_out(RD2_out), .SignExtend_out(Se_out), .Rs_out(Rs_out),
    .Rt_out(Rt_out), .Rd_out(Rd_out), .Control_out(Control_out));
endmodule

module EX_MEM_Pipeline (
  input  clk,
  input  rst,
  input  [31:0] in_3,
  input  [31:0] in_4,
  input  [4:0] in_5,
  input  [3:0] in_6,
  output [31:0] out_7,
  output [31:0] out_8,
  output [4:0] out_9,
  output [3:0] out_10
);

  EX_MEM ex_mem_1 (
    .clk(clk), .rst(rst), .ALUResult_in(in_3), .WriteData_in(in_4), .Rd_in(in_5), .Control_in(in_6),
    .ALUResult_out(out_7), .WriteData_out(out_8), .Rd_out(out_9), .Control_out(out_10));
endmodule

module MEM_WB_Pipeline (
  input  clk,
  input  rst,
  input  [31:0] in_3,
  input  [31:0] in_4,
  input  [4:0] in_5,
  input  [3:0] in_6,
  output [31:0] out_7,
  output [31:0] out_8,
  output [4:0] out_9,
  output [3:0] out_10
);

  MEM_WB mem_wb_1 (
    .clk(clk), .rst(rst), .ReadData_in(in_3), .ALUResult_in(in_4), .Rd_in(in_5), .Control_in(in_6),
    .ReadData_out(out_7), .ALUResult_out(out_8), .Rd_out(out_9), .Control_out(out_10));
endmodule

// VHDL entity somador, as the project stores it:
------------------------------------------------------------------------------------------------------
-- Project : CPU RISC-V DE 32 BITS: DESIGN E IMPLEMENTAÇÃO COM PIPELINE DE 5 ESTÁGIOS
-- File    : ULA
-- Autores : Dhayse Tito, 
--			 Eduardo Guimarães Fr., 
--			 João Pedro Baptista, 
--			 Lígia Calina Bonifácio,
--			 Luiza Lissandra Rosa	
------------------------------------------------------------------------------------------------------
-- Description : Unidade Lógica Aritmética - Realiza operações aritméticas e lógicas nos operandos
------------------------------------------------------------------------------------------------------

library IEEE;
use IEEE.STD_LOGIC_1164.ALL;
use IEEE.STD_LOGIC_ARITH.ALL;
use IEEE.STD_LOGIC_UNSIGNED.ALL;

entity somador is
    Port (
        A       : in  STD_LOGIC_VECTOR(31 downto 0);
        B       : in  STD_LOGIC_VECTOR(31 downto 0);
        Sum     : out STD_LOGIC_VECTOR(31 downto 0)
    );
end somador;

architecture Behavioral of somador is
begin
    Sum <= A + B;
end Behavioral;

// VHDL entity ALU2, as the project stores it:
------------------------------------------------------------------------------------------------------
-- Projeto: CPU RISC-V DE 32 BITS: DESIGN E IMPLEMENTACAO COM PIPELINE DE 5 ESTAGIOS
-- Arquivo: ULA
-- Autores: Dhayse Tito, 
--		    Eduardo Guimaraes Fr., 
--		    Joao Pedro Baptista, 
--		    Ligia Calina Bonifacio e
--		    Luiza Lissandra Rosa	
------------------------------------------------------------------------------------------------------
-- Descricao : Unidade Logica e Aritmetica - ULA
------------------------------------------------------------------------------------------------------

-- Importacoes necessarias
library IEEE;
use IEEE.STD_LOGIC_1164.ALL;
use ieee.numeric_std.ALL;
USE IEEE.std_logic_unsigned.ALL;

-- Definicao da entidade ALU
entity ALU2 is
    Port ( A, B       : in  STD_LOGIC_VECTOR (31 downto 0);
           Control 	  : in  STD_LOGIC_VECTOR (3 downto 0);
           Result     : out STD_LOGIC_VECTOR (31 downto 0);
           Zero       : out STD_LOGIC
         );
end ALU2;

-- Definicao da arquitetura da ALU
architecture Behavioral of ALU2 is

signal Result_aux : std_logic_vector(31 downto 0);
signal Zero_aux   : std_logic_vector(32 downto 0);

-- Implementacao da logica da ALU
begin
    process(A, B, Control)
    begin
        case Control is
            when "0000" =>  -- ADD
                Result_aux <= std_logic_vector(unsigned(A) + unsigned(B));
            when "0001" =>  -- SUB
                Result_aux <= std_logic_vector(unsigned(A) - unsigned(B));
            when "0010" =>  -- AND
                Result_aux <= A and B;
            when "0011" =>  -- OR
                Result_aux <= A or B;
            when "0100" =>  -- XOR
                Result_aux <= A xor B;
            when "0101" =>  -- SLL
                Result_aux <= std_logic_vector(shift_left(unsigned(A), to_integer(unsigned(B(4 downto 0)))));
            when "0110" =>  -- SRL
                Result_aux <= std_logic_vector(shift_right(unsigned(A), to_integer(unsigned(B(4 downto 0)))));
            when others =>
                Result_aux <= (others => '0');
        end case;
        
    end process;

    -- Atribuir valores aos sinais de saida
    Result <= Result_aux;
	     
	-- Inicializacao do sinal Zero_aux
	Zero_aux(0) <= '0';
	
	-- Geracao dos valores Zero_aux
	G2: for I in 1 to 32 generate
	    Zero_aux(I) <= Zero_aux(I - 1) or Result_aux(I - 1);
	end generate;
	
	-- Definicao final do sinal zero
	Zero <= not Zero_aux(32);
    
end Behavioral;

// VHDL entity ALUControl, as the project stores it:
------------------------------------------------------------------------------------------------------
-- Projeto: CPU RISC-V DE 32 BITS: DESIGN E IMPLEMENTACAO COM PIPELINE DE 5 ESTAGIOS
-- Arquivo: Controle da ULA
-- Autores: Dhayse Tito, 
--          Eduardo Guimaraes Fr., 
--          Joao Pedro Baptista, 
--          Ligia Calina Bonifacio e
--          Luiza Lissandra Rosa    
------------------------------------------------------------------------------------------------------
-- Descricao : Controle da Unidade Logica e Aritmetica - ULA
------------------------------------------------------------------------------------------------------

-- Importacoes necessarias
library IEEE;
use IEEE.STD_LOGIC_1164.ALL;
use IEEE.STD_LOGIC_UNSIGNED.ALL;

-- Definicao da entidade Controle da ALU
entity ALUControl is
    Port ( Instr      : in STD_LOGIC_VECTOR (31 downto 0);
           ALUOp      : in  STD_LOGIC_VECTOR (1 downto 0);
           Control    : out STD_LOGIC_VECTOR (3 downto 0) 
          );
end ALUControl;

-- Definicao da arquitetura da ALU
architecture Behavioral of ALUControl is

-- Definicao de sinal auxiliar
signal Control_aux  : STD_LOGIC_VECTOR (3 downto 0);
signal aux1         : STD_LOGIC;  -- Sinal para armazenar Instr[30]
signal aux3         : STD_LOGIC_VECTOR(2 downto 0);  -- Sinal para armazenar Instr[14-12]

-- Implementacao da logica do Controle da ALU
begin

    aux1  <= Instr(30); -- Extrai func7 da instrução
    aux3  <= Instr(14 downto 12); -- Extrai func3 da instrução
    process(aux1, aux3, ALUOp)
    begin
        case ALUOp is
            when "00" =>  -- LW, SW
                Control_aux <= "0000"; -- igual ADD
            when "01" =>  -- BEQ, BNE
                Control_aux <= "0001"; -- igual SUB
            when "10" =>  -- R-Type
                case aux3 is
                    when "000" =>  -- ADD, SUB
                        if aux1 = '0' then
                            Control_aux <= "0000";  -- ADD
                        elsif aux1 = '1' then
                            Control_aux <= "0001";  -- SUB
                        end if;
                    when "111" =>  -- AND
                        Control_aux <= "0010";
                    when "110" =>  -- OR
                        Control_aux <= "0011";
                    when "100" =>  -- XOR
                        Control_aux <= "0100";
                    when "001" =>  -- SLL
                        Control_aux <= "0101";
                    when "101" =>  -- SRL
                        Control_aux <= "0110";
                    when others =>
                        Control_aux <= (others => '0');
                end case;
            when "11" =>  -- I-Type
                case aux3 is
                    when "000" =>  -- ADDI
                        Control_aux <= "0000";
                    when "111" =>  -- ANDI
                        Control_aux <= "0010";
                    when "110" =>  -- ORI
                        Control_aux <= "0011";
                    when "100" =>  -- XORI
                        Control_aux <= "0100";
                    when "001" =>  -- SLLI
                        Control_aux <= "0101";
                    when "101" =>  -- SRLI
                        Control_aux <= "0110";
                    when others =>
                        Control_aux <= (others => '0');
                end case;
            when others =>
                Control_aux <= (others => '0');
        end case;
    end process;

	Control <= Control_aux;
    
end Behavioral;

// VHDL entity ImmGen, as the project stores it:
------------------------------------------------------------------------------------------------------
-- Project : CPU RISC-V DE 32 BITS: DESIGN E IMPLEMENTAÇÃO COM PIPELINE DE 5 ESTÁGIOS
-- File    : ImmGen
-- Autores : Dhayse Tito, 
--			 Eduardo Guimarães Fr., 
--			 João Pedro Baptista, 
--			 Lígia Calina Bonifácio,
--			 Luiza Lissandra Rosa	
------------------------------------------------------------------------------------------------------
-- Description : Extensão de Sinal
------------------------------------------------------------------------------------------------------

library IEEE;
use IEEE.STD_LOGIC_1164.ALL;
USE IEEE.NUMERIC_STD.ALL;

entity ImmGen is
    Port( Instr: in std_logic_vector(31 downto 0);  -- Entrada: instrução de 32 bits
          Imm: out std_logic_vector(31 downto 0)   -- Saída: imediato de 32 bits
        );
end ImmGen;

architecture Behavioral of ImmGen is
    signal opcode       : std_logic_vector(6 downto 0);  -- Sinal para armazenar o opcode da instrução
    signal Imm_aux      : std_logic_vector(31 downto 0) := (others => '0'); -- Inicializa com '0'

begin

    opcode <= Instr(6 downto 0);  -- Extrai o opcode da instrução

    -- Processo para determinar o imediato baseado no opcode
    process(opcode)
    begin
        case opcode is
            when "0010011" | "0000011" => -- I-type (ADDI, ANDI, ORI, XORI, SLLI, SRLI) | (LW)
                Imm_aux(11 downto 0)  <= Instr(31 downto 20);  -- Campo imediato
                Imm_aux(31 downto 12) <= (others => Instr(31)); -- Extensão de sinal
                
            when "1100111" => -- I-type (JALR)
                Imm_aux(11 downto 0)  <= Instr(31 downto 20);  -- Campo imediato
                Imm_aux(31 downto 12) <= (others => Instr(31)); -- Extensão de sinal
                
            when "0100011" => -- S-type (SW)
                Imm_aux(11 downto 5)  <= Instr(31 downto 25);  -- Parte alta do campo imediato
                Imm_aux(4 downto 0)   <= Instr(11 downto 7);   -- Parte baixa do campo imediato
                Imm_aux(31 downto 12) <= (others => Instr(31)); -- Extensão de sinal
                
            when "1100011" => -- SB-type (BEQ, BNE)
                Imm_aux(12)            <= Instr(31);           -- Bit de sinal para o campo imediato
                Imm_aux(10 downto 5)   <= Instr(30 downto 25); -- Bits 10-5 para o campo imediato
                Imm_aux(4 downto 1)    <= Instr(11 downto 8);  -- Bits 4-1 para o campo imediato
                Imm_aux(11)            <= Instr(7);            -- Bit 11 para o campo imediato
                Imm_aux(31 downto 13)  <= (others => Instr(31)); -- Extensão de sinal
                
            when "1101111" => -- UJ-type (JAL)
                Imm_aux(20)            <= Instr(31);           -- Bit 20 para o campo imediato
                Imm_aux(10 downto 1)   <= Instr(30 downto 21); -- Bits 10-1 para o campo imediato
                Imm_aux(11)            <= Instr(20);           -- Bit 11 para o campo imediato
                Imm_aux(19 downto 12)  <= Instr(19 downto 12); -- Bits 19-12 para o campo imediato
                Imm_aux(31 downto 21)  <= (others => Instr(31)); -- Extensão de sinal
                
            when "0110111" | "0010111" => -- U-Type (LUI) | (AUIPC)
                Imm_aux(31 downto 12) <= Instr(31 downto 12); -- Campo imediato
                Imm_aux(11 downto 0)  <= (others => '0');     -- Zero padding

            when others => -- Default para opcode não reconhecido
                Imm_aux <= (others => '0'); -- Zera o imediato se o opcode não for reconhecido
        end case;
    end process;

    -- Saída do imediato
    Imm <= Imm_aux;

end Behavioral;

// VHDL entity PC2, as the project stores it:
------------------------------------------------------------------------------------------------------
-- Projeto: CPU RISC-V DE 32 BITS: DESIGN E IMPLEMENTACAO COM PIPELINE DE 5 ESTAGIOS
-- Arquivo: PC
-- Autores: Dhayse Tito, 
--          Eduardo Guimaraes Fr., 
--          Joao Pedro Baptista, 
--          Ligia Calina Bonifacio e
--          Luiza Lissandra Rosa    
------------------------------------------------------------------------------------------------------
-- Descricao : Program Counter (PC) - Passa a instrução quando o ha um rising clock
------------------------------------------------------------------------------------------------------

-- Importacoes necessarias
library IEEE;
use IEEE.STD_LOGIC_1164.ALL;
use IEEE.STD_LOGIC_ARITH.ALL;
use IEEE.STD_LOGIC_UNSIGNED.ALL;

-- Definicao da entidade PC
entity PC2 is
    Port ( clk    : in  STD_LOGIC;
        	 rst    : in  STD_LOGIC;
        	 PC_in  : in  STD_LOGIC_VECTOR (31 downto 0);
        	 PC_out : out STD_LOGIC_VECTOR (31 downto 0)
    	    );
end PC2;

-- Definicao da arquitetura do PC
architecture Behavioral of PC2 is

-- Definicao de sinal
signal PC_reg : STD_LOGIC_VECTOR (31 downto 0);

-- Implementacao da logica do PC
begin
    process(clk, rst)

    begin
        if rst = '1' then
            PC_reg <= (others => '0');
        elsif rising_edge(clk) then
            PC_reg <= PC_in;
        end if;

    end process;

    PC_out <= PC_reg;

end Behavioral;

// VHDL entity control_unit, as the project stores it:
------------------------------------------------------------------------------------------------------
-- Projeto: CPU RISC-V DE 32 BITS: DESIGN E IMPLEMENTACAO COM PIPELINE DE 5 ESTAGIOS
-- Arquivo: Unidade de controle
-- Autores: Dhayse Tito, 
--          Eduardo Guimaraes Fr., 
--          Joao Pedro Baptista, 
--          Ligia Calina Bonifacio e
--          Luiza Lissandra Rosa    
------------------------------------------------------------------------------------------------------
-- Descricao: Unidade de controle
------------------------------------------------------------------------------------------------------

-- Importacoes necessarias

library IEEE;
use IEEE.STD_LOGIC_1164.ALL;
use IEEE.NUMERIC_STD.ALL;

-- Definição da entidade da unidade de controle
entity control_unit is
    Port(
        Instr     : in std_logic_vector(31 downto 0);  -- Entrada: instrução de 32 bits
        ALUOp     : out std_logic_vector(1 downto 0);  -- EX
        ALUSrc    : out std_logic;
        Branch    : out std_logic;                     -- MEM        
        MemRead   : out std_logic;                     -- MEM        
        MemWrite  : out std_logic;                     -- MEM        
        RegWrite  : out std_logic;                     -- WB        
        MemtoReg  : out std_logic                      -- WB
    );
end control_unit;

-- Definição da arquitetura da unidade de controle
architecture Behavioral of control_unit is

    -- Sinais auxiliares de controle
    signal opcode       : std_logic_vector(6 downto 0);
    signal ALUOp_aux    : std_logic_vector(1 downto 0); -- EX
    signal ALUSrc_aux   : std_logic; -- EX
    signal Branch_aux   : std_logic; -- MEM 
    signal MemRead_aux  : std_logic; -- MEM 
    signal MemWrite_aux : std_logic; -- MEM        
    signal RegWrite_aux : std_logic; -- WB
    signal MemtoReg_aux : std_logic; -- WB
   
begin
    opcode <= Instr(6 downto 0);  -- Extrai o opcode da instrução
    
    process(opcode)
    begin
        -- Valores padrão para sinais de controle
        ALUOp_aux    <= "00";
        ALUSrc_aux   <= '0';
        Branch_aux   <= '0';
        MemRead_aux  <= '0';
        MemWrite_aux <= '0';
        RegWrite_aux <= '0';
        MemtoReg_aux <= '0';

        case opcode is
            when "0110011"  => -- R-Type
                ALUOp_aux    <= "10";
                ALUSrc_aux   <= '0';
                RegWrite_aux <= '1';

            when "0000011" => -- I-Type (LW)
                ALUOp_aux    <= "00";
                ALUSrc_aux   <= '1';
                MemRead_aux  <= '1';
                MemtoReg_aux <= '1';
                RegWrite_aux <= '1';

            when "0100011" => -- S-Type (SW)
                ALUOp_aux    <= "00";
                ALUSrc_aux   <= '1';
                MemWrite_aux <= '1';

            when "1100011" => -- SB-Type (BEQ)
                ALUOp_aux    <= "01";
                ALUSrc_aux   <= '0';
                Branch_aux   <= '1';

            when others =>
                -- Valores padrão para sinais de controle em caso de opcode não reconhecido
                ALUOp_aux    <= "00";
                ALUSrc_aux   <= '0';
                Branch_aux   <= '0';
                MemRead_aux  <= '0';
                MemWrite_aux <= '0';
                RegWrite_aux <= '0';
                MemtoReg_aux <= '0';
        end case;
    end process;

    -- Atribuições de saída
    ALUOp    <= ALUOp_aux;
    ALUSrc   <= ALUSrc_aux;
    Branch   <= Branch_aux;
    MemRead  <= MemRead_aux;
    MemWrite <= MemWrite_aux; 
    RegWrite <= RegWrite_aux;
    MemtoReg <= MemtoReg_aux;

end Behavioral;

// VHDL entity IF_ID_Pipe, as the project stores it:
------------------------------------------------------------------------------------------------------
-- Projeto: CPU RISC-V DE 32 BITS: DESIGN E IMPLEMENTACAO COM PIPELINE DE 5 ESTAGIOS
-- Arquivo: IF_ID
-- Autores: Dhayse Tito, 
--          Eduardo Guimaraes Fr., 
--          Joao Pedro Baptista, 
--          Ligia Calina Bonifacio e
--          Luiza Lissandra Rosa    
------------------------------------------------------------------------------------------------------
-- Descricao: IF_ID
------------------------------------------------------------------------------------------------------

library IEEE;
use IEEE.STD_LOGIC_1164.ALL;
use IEEE.STD_LOGIC_ARITH.ALL;
use IEEE.STD_LOGIC_UNSIGNED.ALL;

entity IF_ID_Pipe is
    Port (
        clk             : in  STD_LOGIC;
        rst             : in  STD_LOGIC;
        IF_ID_Write     : in  STD_LOGIC; -- Forward
        IF_ID_Flush     : in  STD_LOGIC; -- Hazard
        PC_in           : in  STD_LOGIC_VECTOR(31 downto 0);
        PC_4_in         : in  STD_LOGIC_VECTOR(63 downto 0);
        Instr_in        : in  STD_LOGIC_VECTOR(31 downto 0);
        PC_out          : out STD_LOGIC_VECTOR(31 downto 0);
        PC_4_out        : out STD_LOGIC_VECTOR(63 downto 0);
        Instr_out       : out STD_LOGIC_VECTOR(31 downto 0)
    );
end IF_ID_Pipe;

architecture Behavioral of IF_ID_Pipe is
    signal PC_reg      : STD_LOGIC_VECTOR(31 downto 0);
    signal PC_4_reg    : STD_LOGIC_VECTOR(63 downto 0);
    signal Instr_reg   : STD_LOGIC_VECTOR(31 downto 0);
begin
    process(clk, rst)
    begin
        if rst = '1' then
            PC_reg <= (others => '0');
            PC_4_reg <= (others => '0');
            Instr_reg <= (others => '0');
        elsif rising_edge(clk) then
            if IF_ID_Flush = '1' then
                PC_reg <= (others => '0');
                PC_4_reg <= (others => '0');
                Instr_reg <= (others => '0');
            elsif IF_ID_Write = '1' then
                PC_reg <= PC_in;
                PC_4_reg <= PC_4_in;
                Instr_reg <= Instr_in;
            end if;
        end if;
    end process;

    PC_out <= PC_reg;
    PC_4_out <= PC_4_reg;
    Instr_out <= Instr_reg;
end Behavioral;

// VHDL entity ID_EX, as the project stores it:
------------------------------------------------------------------------------------------------------
-- Projeto: CPU RISC-V DE 32 BITS: DESIGN E IMPLEMENTACAO COM PIPELINE DE 5 ESTAGIOS
-- Arquivo: ID_EX
-- Autores: Dhayse Tito, 
--          Eduardo Guimaraes Fr., 
--          Joao Pedro Baptista, 
--          Ligia Calina Bonifacio e
--          Luiza Lissandra Rosa    
------------------------------------------------------------------------------------------------------
-- Descricao : ID_EX
------------------------------------------------------------------------------------------------------

library IEEE;
use IEEE.STD_LOGIC_1164.ALL;
use IEEE.STD_LOGIC_ARITH.ALL;
use IEEE.STD_LOGIC_UNSIGNED.ALL;

entity ID_EX is
    Port (
        clk             : in  STD_LOGIC;
        rst             : in  STD_LOGIC;
        -- sinais de entrada
        PC_in           : in  STD_LOGIC_VECTOR(31 downto 0);
        ReadData1_in    : in  STD_LOGIC_VECTOR(31 downto 0);
        ReadData2_in    : in  STD_LOGIC_VECTOR(31 downto 0);
        SignExtend_in   : in  STD_LOGIC_VECTOR(31 downto 0);
        Rs_in           : in  STD_LOGIC_VECTOR(4 downto 0);
        Rt_in           : in  STD_LOGIC_VECTOR(4 downto 0);
        Rd_in           : in  STD_LOGIC_VECTOR(4 downto 0);
        Control_in      : in  STD_LOGIC_VECTOR(3 downto 0); 
        -- sinais de saida
        PC_out          : out STD_LOGIC_VECTOR(31 downto 0);
        ReadData1_out   : out STD_LOGIC_VECTOR(31 downto 0);
        ReadData2_out   : out STD_LOGIC_VECTOR(31 downto 0);
        SignExtend_out  : out STD_LOGIC_VECTOR(31 downto 0);
        Rs_out          : out STD_LOGIC_VECTOR(4 downto 0);
        Rt_out          : out STD_LOGIC_VECTOR(4 downto 0);
        Rd_out          : out STD_LOGIC_VECTOR(4 downto 0);
        Control_out     : out STD_LOGIC_VECTOR(3 downto 0)
    );
end ID_EX;

architecture Behavioral of ID_EX is
    signal PC_reg           : STD_LOGIC_VECTOR(31 downto 0);
    signal ReadData1_reg    : STD_LOGIC_VECTOR(31 downto 0);
    signal ReadData2_reg    : STD_LOGIC_VECTOR(31 downto 0);
    signal SignExtend_reg   : STD_LOGIC_VECTOR(31 downto 0);
    signal Rs_reg           : STD_LOGIC_VECTOR(4 downto 0);
    signal Rt_reg           : STD_LOGIC_VECTOR(4 downto 0);
    signal Rd_reg           : STD_LOGIC_VECTOR(4 downto 0);
    signal Control_reg      : STD_LOGIC_VECTOR(3 downto 0);
begin
    process(clk, rst)
    begin
        if rst = '1' then
            PC_reg <= (others => '0');
            ReadData1_reg <= (others => '0');
            ReadData2_reg <= (others => '0');
            SignExtend_reg <= (others => '0');
            Rs_reg <= (others => '0');
            Rt_reg <= (others => '0');
            Rd_reg <= (others => '0');
            Control_reg <= (others => '0');
        elsif rising_edge(clk) then
            PC_reg <= PC_in;
            ReadData1_reg <= ReadData1_in;
            ReadData2_reg <= ReadData2_in;
            SignExtend_reg <= SignExtend_in;
            Rs_reg <= Rs_in;
            Rt_reg <= Rt_in;
            Rd_reg <= Rd_in;
            Control_reg <= Control_in;
        end if;
    end process;

    PC_out <= PC_reg;
    ReadData1_out <= ReadData1_reg;
    ReadData2_out <= ReadData2_reg;
    SignExtend_out <= SignExtend_reg;
    Rs_out <= Rs_reg;
    Rt_out <= Rt_reg;
    Rd_out <= Rd_reg;
    Control_out <= Control_reg;
end Behavioral;

// VHDL entity EX_MEM, as the project stores it:
------------------------------------------------------------------------------------------------------
-- Projeto: CPU RISC-V DE 32 BITS: DESIGN E IMPLEMENTACAO COM PIPELINE DE 5 ESTAGIOS
-- Arquivo: EX MEM
-- Autores: Dhayse Tito, 
--          Eduardo Guimaraes Fr., 
--          Joao Pedro Baptista, 
--          Ligia Calina Bonifacio e
--          Luiza Lissandra Rosa    
------------------------------------------------------------------------------------------------------
-- Descricao: EX_MEM
------------------------------------------------------------------------------------------------------

library IEEE;
use IEEE.STD_LOGIC_1164.ALL;
use IEEE.STD_LOGIC_ARITH.ALL;
use IEEE.STD_LOGIC_UNSIGNED.ALL;

entity EX_MEM is
    Port (
        clk             : in  STD_LOGIC;
        rst             : in  STD_LOGIC;
        ALUResult_in    : in  STD_LOGIC_VECTOR(31 downto 0);
        WriteData_in    : in  STD_LOGIC_VECTOR(31 downto 0);
        Rd_in           : in  STD_LOGIC_VECTOR(4 downto 0);
        Control_in      : in  STD_LOGIC_VECTOR(3 downto 0); 
        ALUResult_out   : out STD_LOGIC_VECTOR(31 downto 0);
        WriteData_out   : out STD_LOGIC_VECTOR(31 downto 0);
        Rd_out          : out STD_LOGIC_VECTOR(4 downto 0);
        Control_out     : out STD_LOGIC_VECTOR(3 downto 0)
    );
end EX_MEM;

architecture Behavioral of EX_MEM is
    signal ALUResult_reg   : STD_LOGIC_VECTOR(31 downto 0);
    signal WriteData_reg   : STD_LOGIC_VECTOR(31 downto 0);
    signal Rd_reg          : STD_LOGIC_VECTOR(4 downto 0);
    signal Control_reg     : STD_LOGIC_VECTOR(3 downto 0);
begin
    process(clk, rst)
    begin
        if rst = '1' then
            ALUResult_reg <= (others => '0');
            WriteData_reg <= (others => '0');
            Rd_reg <= (others => '0');
            Control_reg <= (others => '0');
        elsif rising_edge(clk) then
            ALUResult_reg <= ALUResult_in;
            WriteData_reg <= WriteData_in;
            Rd_reg <= Rd_in;
            Control_reg <= Control_in;
        end if;
    end process;

    ALUResult_out <= ALUResult_reg;
    WriteData_out <= WriteData_reg;
    Rd_out <= Rd_reg;
    Control_out <= Control_reg;
end Behavioral;

// VHDL entity MEM_WB, as the project stores it:
------------------------------------------------------------------------------------------------------
-- Projeto: CPU RISC-V DE 32 BITS: DESIGN E IMPLEMENTACAO COM PIPELINE DE 5 ESTAGIOS
-- Arquivo: MEM_WB
-- Autores: Dhayse Tito, 
--          Eduardo Guimaraes Fr., 
--          Joao Pedro Baptista, 
--          Ligia Calina Bonifacio e
--          Luiza Lissandra Rosa    
------------------------------------------------------------------------------------------------------
-- Descricao: MEM_WB
------------------------------------------------------------------------------------------------------


library IEEE;
use IEEE.STD_LOGIC_1164.ALL;
use IEEE.STD_LOGIC_ARITH.ALL;
use IEEE.STD_LOGIC_UNSIGNED.ALL;

entity MEM_WB is
    Port (
        clk             : in  STD_LOGIC;
        rst             : in  STD_LOGIC;
        ReadData_in     : in  STD_LOGIC_VECTOR(31 downto 0);
        ALUResult_in    : in  STD_LOGIC_VECTOR(31 downto 0);
        Rd_in           : in  STD_LOGIC_VECTOR(4 downto 0);
        Control_in      : in  STD_LOGIC_VECTOR(3 downto 0);
        ReadData_out    : out STD_LOGIC_VECTOR(31 downto 0);
        ALUResult_out   : out STD_LOGIC_VECTOR(31 downto 0);
        Rd_out          : out STD_LOGIC_VECTOR(4 downto 0);
        Control_out     : out STD_LOGIC_VECTOR(3 downto 0)
    );
end MEM_WB;

architecture Behavioral of MEM_WB is
    signal ReadData_reg    : STD_LOGIC_VECTOR(31 downto 0);
    signal ALUResult_reg   : STD_LOGIC_VECTOR(31 downto 0);
    signal Rd_reg          : STD_LOGIC_VECTOR(4 downto 0);
    signal Control_reg     : STD_LOGIC_VECTOR(3 downto 0);
begin
    process(clk, rst)
    begin
        if rst = '1' then
            ReadData_reg <= (others => '0');
            ALUResult_reg <= (others => '0');
            Rd_reg <= (others => '0');
            Control_reg <= (others => '0');
        elsif rising_edge(clk) then
            ReadData_reg <= ReadData_in;
            ALUResult_reg <= ALUResult_in;
            Rd_reg <= Rd_in;
            Control_reg <= Control_in;
        end if;
    end process;

    ReadData_out <= ReadData_reg;
    ALUResult_out <= ALUResult_reg;
    Rd_out <= Rd_reg;
    Control_out <= Control_reg;
end Behavioral;
